// Logisim project Relatório 1.circ as structural Verilog
module _1__Circuito_A___0__A (
  input  in_1,
  output out_2
);

  or or_1 (out_2, in_1, 1'b0);
endmodule

module _2__Circuito_A___A___A (
  input  in_1,
  output out_2
);

  or or_1 (out_2, in_1, in_1);
endmodule

module _3__Circuito_A___AB___A (
  input  in_1,
  input  in_2,
  output out_3
);

  wire and_1_out;

  and and_1 (and_1_out, in_1, in_2);
  or or_1 (out_3, in_1, and_1_out);
endmodule

module _4__Circuito_A____AB___A___B (
  input  in_1,
  input  in_2,
  output out_3
);

  wire and_1_out, not_1_out;

  not not_1 (not_1_out, in_1);
  and and_1 (and_1_out, not_1_out, in_2);
  or or_1 (out_3, in_1, and_1_out);
endmodule

module _5__Circuito_A___1___1 (
  input  in_1,
  output out_2
);

  or or_1 (out_2, in_1, 1'b1);
endmodule

module _6__Circuito__A___A___1 (
  input  in_1,
  output out_2
);

  wire not_1_out;

  not not_1 (not_1_out, in_1);
  or or_1 (out_2, in_1, not_1_out);
endmodule

module _7__Circuito_AB____AB___A (
  input  in_1,
  input  in_2,
  output out_3
);

  wire and_1_out, and_2_out, not_1_out;

  not not_1 (not_1_out, in_2);
  and and_1 (and_1_out, in_1, in_2);
  and and_2 (and_2_out, not_1_out, in_1);
  or or_1 (out_3, and_1_out, and_2_out);
endmodule

module _8__Circuito_A___BC____A___B_____A___C (
  input  in_1,
  input  in_2,
  input  in_3,
  output out_4
);

  wire and_1_out;

  and and_1 (and_1_out, in_2, in_3);
  or or_1 (out_4, in_1, and_1_out);
endmodule

module _9__Habilita_Dado (
  input  in_1,
  input  in_2,
  input  in_3,
  input  in_4,
  input  in_5,
  input  in_6,
  input  in_7,
  input  in_8,
  output out_9,
  output out_10,
  output out_11,
  output out_12
);

  and and_1 (out_9, in_1, in_2);
  and and_2 (out_10, in_3, in_4);
  and and_3 (out_11, in_5, in_6);
  and and_4 (out_12, in_7, in_8);
endmodule
