// Logisim project Relatório 2.circ as structural Verilog
module \_1__Qual_é_a_função_equivalente  (
  input  in_1,
  output out_2
);

  nand nand_1 (out_2, in_1, in_1);
endmodule

module \_2__Qual_é_a_função_equivalente  (
  input  in_1,
  output out_2
);

  nor nor_1 (out_2, in_1, in_1);
endmodule

module \_3__Qual_é_a_função_equivalente  (
  input  in_1,
  input  in_2,
  output out_3
);

  wire nand_1_out;

  nand nand_1 (nand_1_out, in_1, in_2);
  nand nand_2 (out_3, nand_1_out, nand_1_out);
endmodule

module \_4__Qual_é_a_função_equivalente  (
  input  in_1,
  input  in_2,
  output out_3
);

  wire nor_1_out;

  nor nor_1 (nor_1_out, in_1, in_2);
  nor nor_2 (out_3, nor_1_out, nor_1_out);
endmodule

module \_5__Qual_é_a_função_equivalente  (
  input  in_1,
  input  in_2,
  output out_3
);

  wire nand_1_out, nand_2_out;

  nand nand_1 (nand_1_out, in_1, in_1);
  nand nand_2 (nand_2_out, in_2, in_2);
  nand nand_3 (out_3, nand_1_out, nand_2_out);
endmodule

module \_6__Qual_é_a_função_equivalente  (
  input  in_1,
  input  in_2,
  output out_3
);

  wire nor_1_out, nor_2_out;

  nor nor_1 (nor_1_out, in_1, in_1);
  nor nor_2 (nor_2_out, in_2, in_2);
  nor nor_3 (out_3, nor_1_out, nor_2_out);
endmodule

module \_7__Qual_é_a_função_equivalente  (
  input  in_1,
  input  in_2,
  output out_3
);

  wire nand_1_out, nand_2_out, nand_3_out;

  nand nand_1 (nand_1_out, in_1, in_1);
  nand nand_2 (nand_2_out, in_2, in_2);
  nand nand_3 (nand_3_out, nand_1_out, nand_2_out);
  nand nand_4 (out_3, nand_3_out, nand_3_out);
endmodule

module \_8__Qual_é_a_função_equivalente  (
  input  in_1,
  input  in_2,
  output out_3
);

  wire nor_1_out, nor_2_out, nor_3_out;

  nor nor_1 (nor_1_out, in_1, in_1);
  nor nor_2 (nor_2_out, in_2, in_2);
  nor nor_3 (nor_3_out, nor_1_out, nor_2_out);
  nor nor_4 (out_3, nor_3_out, nor_3_out);
endmodule

module \_9__Qual_é_a_função_equivalente  (
  input  in_1,
  input  in_2,
  input  in_3,
  input  in_4,
  input  in_5,
  input  in_6,
  output out_7,
  output out_8
);

  wire nand_1_out, nand_2_out, nand_3_out, nand_4_out, or_1_out;

  or or_1 (or_1_out, in_1, in_2);
  nand nand_1 (nand_1_out, in_4, in_4);
  nand nand_2 (nand_2_out, in_5, in_5);
  and and_1 (out_7, or_1_out, in_3);
  nand nand_3 (nand_3_out, nand_1_out, nand_2_out);
  nand nand_4 (nand_4_out, nand_3_out, in_6);
  nand nand_5 (out_8, nand_4_out, nand_4_out);
endmodule

module \_10__Experiência_1  (
  input  in_1,
  input  in_2,
  input  in_3,
  output out_4
);

  wire and_1_out, not_1_out, or_1_out, or_2_out;

  not not_1 (not_1_out, in_3);
  or or_1 (or_1_out, in_1, in_2);
  and and_1 (and_1_out, in_2, not_1_out);
  or or_2 (or_2_out, or_1_out, and_1_out);
  not not_2 (out_4, or_2_out);
endmodule

module \_11__Experiência_2  (
  input  in_1,
  input  in_2,
  output out_3
);

  wire nand_1_out, nand_2_out, nand_3_out;

  nand nand_1 (nand_1_out, in_1, in_2);
  nand nand_2 (nand_2_out, in_1, nand_1_out);
  nand nand_3 (nand_3_out, nand_1_out, in_2);
  nand nand_4 (out_3, nand_2_out, nand_3_out);
endmodule
