// Logisim project Relatório 3.circ as structural Verilog
module _1__Acende_o_Led (
  input  in_1,
  input  in_2,
  input  in_3,
  input  in_4,
  input  in_5,
  input  in_6,
  output out_7,
  output out_8,
  output out_9
);

  wire and_1_out, and_2_out, and_3_out, and_4_out, and_5_out, xor_2_out;

  xor xor_1 (out_7, in_1, in_2);
  xnor xnor_1 (out_8, in_1, in_2);
  and and_1 (and_1_out, in_3, in_4);
  and and_2 (and_2_out, in_4, in_5);
  and and_3 (and_3_out, in_4, in_3);
  and and_4 (and_4_out, in_4, in_3);
  ExactlyOne xor_2 (.out(xor_2_out), .in0(and_1_out), .in1(and_2_out), .in3(and_3_out), .in4(and_4_out));
  and and_5 (and_5_out, in_3, in_5, in_4, in_6);
  or or_1 (out_9, xor_2_out, and_5_out);
endmodule

module \_2__Números_Binários  (
  input  [1:0] in_1,
  input  [1:0] in_2,
  output out_3,
  output out_4,
  output out_5
);

  Comparator #(.width(2)) comparator_1 (.a(in_1), .b(in_2), .gt(out_5), .eq(out_4), .lt(out_3));
endmodule

module \_3__Aprovação  (
  input  in_1,
  input  in_2,
  input  in_3,
  output out_4
);

  wire and_1_out, and_2_out, and_3_out;

  and and_1 (and_1_out, in_1, in_2);
  and and_2 (and_2_out, in_1, in_2, in_3);
  and and_3 (and_3_out, in_1, in_3);
  or or_1 (out_4, and_1_out, and_2_out, and_3_out);
endmodule

module \_4__Controle_de_Conexão  (
  input  in_1,
  input  in_2,
  input  in_3,
  output [2:0] out_4
);

  Priority_Encoder priority_encoder_1 (
    .in1(in_1), .in3(in_2), .in5(in_3), .out(out_4));  // open: in0, in2, in4, in6, in7, en_in, gs, en_out
endmodule
